# Fritzing sketch control mechanism (saved by Fritzing 0.9.6b)

parts:
  Part1 = Arduino Uno (Rev3) - ICSP
  Mod1 = KY-019 5V Relay Module [package="Breakout board"]
  M1 = DC Motor  # not connected
  JACK1 = 2.1mm Barrel Jack with Terminal Block
  JACK2 = 2.1mm Barrel Jack with Terminal Block
  TRM1 = Terminal 2pin  # not connected
  TRM2 = Terminal 2pin

nets:
  N1: Part1.D13/SCK, Mod1.S
  N2: Part1.GND, Mod1.-
  N3: Part1.5V, Mod1.+
  N4: Mod1.Common, JACK2.POS
  N5: JACK1.POS, TRM2.pin_1
  N6: JACK1.NEG, TRM2.pin_2

custom parts:
  KY-019 5V Relay Module: KY-019 5V Relay module, used to control AC circuits. (Special thanks to vanepp for fixing the PCB holes and other errors)
  Terminal 2pin: 2-pin Terminal Block
