# Fritzing sketch pendulum (saved by Fritzing 0.9.6b)

parts:
  Part1 = Arduino Nano 33 IOT
  Part2 = Bi-Directional Logic Level Converter [part_number=BOB-12009]
  Part3 = 9-DOF Absolute Orientation IMU Fusion Breakout - BNO055
  Part4 = Adafruit PowerBoost 1000C [part_number="Adafruit #2465"]
  S1 = Toggle Switch [package=THT]
  U1 = LIPO-110mAh [package=lipo-110]  # not connected
  U2 = WS2812 RGB LED strip

nets:
  GND: Part1.GND, Part1.D13~, Part2.GND, Part3.GND, U2.GND
  N1: Part1.A5, Part3.SCL_5V
  N2: Part1.A4, Part3.SDA_5V
  N3: Part1.A2, Part2.LV1
  N4: Part1.3V3, Part3.5.0V
  N5: Part2.HV, U2.VCC
  N6: Part2.HV1, U2.DOUT
  N7: Part4.VBAT, S1.COM
  N8: Part4.ENABLE, S1.L1
  N9: Part4.GND, S1.L2

custom parts:
  Arduino Nano 33 IOT: The Arduino Nano 33 IoT is the easiest and cheapest point of entry to enhance existing devices (and creating new ones) to be part of the IoT and designing pico-network applications. Whether you are looking at building a sensor network connected to your office or home router, or if you want to create a BLE device sending data to a cellphone, the Nano 33 IoT is your one-stop-solution for many of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
  Bi-Directional Logic Level Converter: Description: If you've ever tried to connect a 3.3V device to a 5V system, you know what a challenge it can be. The SparkFun bi-directional logic level converter is a small device that safely steps down 5V signals to 3.3V AND steps up 3.3V to 5V at the same time. This level converter also works with 2.8V and 1.8V devices. What really separates this Logic level converter from our previous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
  9-DOF Absolute Orientation IMU Fusion Breakout - BNO055: A MEMS accelerometer, magnetometer and gyroscope on a single die with a high speed ARM Cortex-M0 based processor to digest all the sensor data, abstract the sensor fusion and real time requirements away, and spit out data you can use in quaternions, Euler angles or vectors.
  Adafruit PowerBoost 1000C: PowerBoost 1000C is the perfect power supply for your portable project! With a built-in load-sharing battery charger circuit, you'll be able to keep your power-hungry project running even while recharging the battery! This little DC/DC boost converter module can be powered by any 3.7V LiIon/LiPoly battery, and convert the battery output to 5.2V DC for running your 5V projects.
  WS2812 RGB LED strip: WS2812 strip
